# Fritzing sketch Schematic (saved by Fritzing 0.9.10b)
breadboards: 1

parts:
  Part1 = Arduino Uno (Rev3)
  R1 = PHOTOCELL [package=photocell-kit]
  R2 = Resistor [tolerance=±5% resistance=220 package="0805 [SMD]"]

nets:
  N1: Part1.A0, R1.P$2, R2.Pin_0
  N2: Part1.5V, R1.P$1
  N3: Part1.GND, R2.Pin_1
